// Logisim project ALU.circ as structural Verilog: 1 circuit, main circuit ALU
module ALU (
  input  [31:0] A,
  input  [31:0] B,
  input  [4:0] Shift,
  input  [3:0] Codop,
  input  CarryIn,
  output [31:0] S,
  output [3:0] Flags
);

  wire AddC, adder_1_cout, bitselector_3_out, bitselector_4_out, bitselector_6_out, bitselector_7_out, cCMN,
       cCMP, comparator_2_eq, MinusShift, not_1_out, not_2_out, not_3_out, not_4_out, opShift, signeA,
       signeB, SubC, subtractor_3_bout, subtractor_5_bout, vAdd, vSub, xnor_1_out, xor_1_out;
  wire [3:0] adder_2_out;
  wire [4:0] subtractor_1_out, subtractor_2_out;
  wire [30:0] multiplexer_1_out;
  wire [31:0] A_AND_B, A_XOR_B, ADC, B_LSL, B_LSR, B_LSR_ARITH, B_LSR_ROT, BIC, CMN, CMP, MUL, MVN,
       not_6_out, ORR, RSB, SBC;

  Multiplexer #(.enable("true"), .select(4), .width(32)) multiplexer_1 (
    .in0(S), .in1(S), .in2(S), .in3(S), .in4(S), .in5(S), .in6(S), .in7(S), .in8(A_AND_B), .in9(S),
    .in10(CMP), .in11(CMN), .in12(S), .in13(S), .in14(S), .in15(S), .out({Flags[3], multiplexer_1_out}),
    .sel(Codop));  // open: en
  BitSelector #(.width(32)) bitselector_1 (.in(A), .out(signeA), .sel({5{1'b1}}));
  BitSelector #(.width(32)) bitselector_2 (.in(B), .out(signeB), .sel({5{1'b1}}));
  Comparator #(.width(32)) comparator_1 (
    .a({32{1'b0}}), .b({Flags[3], multiplexer_1_out}), .eq(Flags[2]));  // open: gt, lt
  Subtractor #(.width(5)) subtractor_1 (.a({5{1'b0}}), .b(Shift), .out(subtractor_1_out));  // open: bin, bout
  Subtractor #(.width(5)) subtractor_2 (.a(Shift), .b(5'b00001), .out(subtractor_2_out));  // open: bin, bout
  BitSelector #(.width(32)) bitselector_3 (.in(CMN), .out(bitselector_3_out), .sel({5{1'b1}}));
  Adder #(.width(32)) adder_1 (.a(MVN), .b(32'h1), .cout(adder_1_cout));  // open: out, cin
  BitSelector #(.width(32)) bitselector_4 (.in(B), .out(bitselector_4_out), .sel(subtractor_1_out));
  xnor xnor_1 (xnor_1_out, signeA, signeB);
  xor xor_1 (xor_1_out, bitselector_3_out, signeB);
  BitSelector #(.width(32)) bitselector_5 (.in(B), .out(MinusShift), .sel(subtractor_2_out));
  and and_1 (vAdd, xnor_1_out, xor_1_out);
  BitSelector #(.width(32)) bitselector_6 (.in(SBC), .out(bitselector_6_out), .sel({5{1'b1}}));
  Multiplexer multiplexer_2 (.in0(bitselector_4_out), .in1(MinusShift), .out(opShift), .sel(not_2_out));
  Adder #(.width(4)) adder_2 (.a(Codop), .b(4'b0001), .out(adder_2_out));  // open: cin, cout
  not not_1 (not_1_out, xnor_1_out);
  Comparator #(.width(1)) comparator_2 (.a(signeB), .b(bitselector_6_out), .eq(comparator_2_eq));  // open: gt, lt
  not not_2 (not_2_out, bitselector_7_out);
  BitSelector #(.width(4)) bitselector_7 (.in(adder_2_out), .out(bitselector_7_out), .sel(2'b01));
  and and_2 (vSub, not_1_out, not_3_out);
  not not_3 (not_3_out, comparator_2_eq);
  Multiplexer #(.select(4), .width(32)) multiplexer_3 (
    .in0(A_AND_B), .in1(A_XOR_B), .in2(B_LSL), .in3(B_LSR), .in4(B_LSR_ARITH), .in5(ADC), .in6(SBC),
    .in7(B_LSR_ROT), .in8(B), .in9(RSB), .in10(B), .in11(B), .in12(ORR), .in13(MUL), .in14(BIC), .in15(MVN),
    .out(S), .sel(Codop));
  Multiplexer #(.select(4)) multiplexer_4 (
    .in0(1'b0), .in1(1'b0), .in2(opShift), .in3(opShift), .in4(opShift), .in5(AddC), .in6(SubC),
    .in7(MinusShift), .in8(1'b0), .in9(adder_1_cout), .in10(cCMP), .in11(cCMN), .in12(1'b0), .in13(1'b0),
    .in14(1'b0), .in15(1'b0), .out(Flags[1]), .sel(Codop));
  assign A_XOR_B = A ^ B;  // XOR_Gate xor_2, 32 bits wide
  Multiplexer #(.select(4)) multiplexer_5 (
    .in0(1'b0), .in1(1'b0), .in2(1'b0), .in3(1'b0), .in4(1'b0), .in5(vAdd), .in6(vSub), .in7(1'b0),
    .in8(1'b0), .in9(1'b0), .in10(vSub), .in11(vAdd), .in12(1'b0), .in13(1'b0), .in14(1'b0), .in15(1'b0),
    .out(Flags[0]), .sel(Codop));
  assign A_AND_B = A & B;  // AND_Gate and_3, 32 bits wide
  Shifter #(.width(32)) shifter_1 (.in(B), .\dist (Shift), .out(B_LSL));
  Shifter #(.shift("lr"), .width(32)) shifter_2 (.in(B), .\dist (Shift), .out(B_LSR));
  Shifter #(.shift("ar"), .width(32)) shifter_3 (.in(B), .\dist (Shift), .out(B_LSR_ARITH));
  Adder #(.width(32)) adder_3 (.a(A), .b(B), .out(ADC), .cin(CarryIn), .cout(AddC));
  not not_4 (not_4_out, CarryIn);
  Subtractor #(.width(32)) subtractor_3 (.a(B), .b(A), .out(SBC), .bin(not_4_out), .bout(subtractor_3_bout));
  not not_5 (SubC, subtractor_3_bout);
  Shifter #(.shift("rr"), .width(32)) shifter_4 (.in(B), .\dist (Shift), .out(B_LSR_ROT));
  // AND_Gate and_4 has open pins: in0=A, in1=B, out=open
  Subtractor #(.width(32)) subtractor_4 (.a({32{1'b0}}), .b(A), .out(RSB));  // open: bin, bout
  Subtractor #(.width(32)) subtractor_5 (.a(B), .b(A), .out(CMP), .bout(subtractor_5_bout));  // open: bin
  Adder #(.width(32)) adder_4 (.a(A), .b(B), .out(CMN), .cout(cCMN));  // open: cin
  assign not_6_out = ~A;  // NOT_Gate not_6, 32 bits wide
  assign MVN = ~A;  // NOT_Gate not_7, 32 bits wide
  not not_8 (cCMP, subtractor_5_bout);
  assign ORR = A | B;  // OR_Gate or_1, 32 bits wide
  Multiplier #(.width(32)) multiplier_1 (.a(A), .b(B), .out(MUL));  // open: cin, cout
  assign BIC = B & not_6_out;  // AND_Gate and_5, 32 bits wide

  // Other names for the same wires on the sheet: cIn = CarryIn; V = Flags[0]; C = Flags[1]; Z = Flags[2];
  //   Sortie[31:0] = S

  // Notes on the sheet:
  //   Note: for ROR, C = N
  //   Note 2: assume that shift > 0 for LSL and LSR
endmodule
