// Logisim project BancDeRegistres.circ as structural Verilog: 1 circuit, main circuit BancRegistre
module BancRegistre (
  input  [31:0] DataIn,
  input  [2:0] RegA,
  input  [2:0] RegB,
  input  [2:0] RegDest,
  input  Clk,
  input  Reset,
  output [31:0] AOut,
  output [31:0] BOut,
  output [31:0] R0,
  output [31:0] R1,
  output [31:0] R2,
  output [31:0] R3,
  output [31:0] R4,
  output [31:0] R5,
  output [31:0] R6,
  output [31:0] R7
);

  wire R0_In, R1_In, R2_In, R3_In, R4_In, R5_In, R6_In, R7_In;

  Decoder #(.select(3)) decoder_1 (
    .out0(R0_In), .out1(R1_In), .out2(R2_In), .out3(R3_In), .out4(R4_In), .out5(R5_In), .out6(R6_In),
    .out7(R7_In), .sel(RegDest));  // open: en
  Multiplexer #(.select(3), .width(32)) multiplexer_1 (
    .in0(R0), .in1(R1), .in2(R2), .in3(R3), .in4(R4), .in5(R5), .in6(R6), .in7(R7), .out(AOut), .sel(RegA));
  Register #(.width(32)) RegistreR0 (.D(DataIn), .en(R0_In), .clk(Clk), .Q(R0), .clr(Reset));
  Register #(.width(32)) RegisterR1 (.D(DataIn), .en(R1_In), .clk(Clk), .Q(R1), .clr(Reset));
  Register #(.width(32)) RegisterR2 (.D(DataIn), .en(R2_In), .clk(Clk), .Q(R2), .clr(Reset));
  Register #(.width(32)) RegisterR3 (.D(DataIn), .en(R3_In), .clk(Clk), .Q(R3), .clr(Reset));
  Register #(.width(32)) RegisterR4 (.D(DataIn), .en(R4_In), .clk(Clk), .Q(R4), .clr(Reset));
  Register #(.width(32)) RegisterR5 (.D(DataIn), .en(R5_In), .clk(Clk), .Q(R5), .clr(Reset));
  Register #(.width(32)) RegisterR6 (.D(DataIn), .en(R6_In), .clk(Clk), .Q(R6), .clr(Reset));
  Register #(.width(32)) RegisterR7 (.D(DataIn), .en(R7_In), .clk(Clk), .Q(R7), .clr(Reset));
  Multiplexer #(.select(3), .width(32)) multiplexer_2 (
    .in0(R0), .in1(R1), .in2(R2), .in3(R3), .in4(R4), .in5(R5), .in6(R6), .in7(R7), .out(BOut), .sel(RegB));

  // Other names for the same wires on the sheet: Clock = Clk; Rst = Reset; RV0[31:0] = R0; RV1[31:0] = R1;
  //   RV2[31:0] = R2; RV3[31:0] = R3; RV4[31:0] = R4; RV5[31:0] = R5; RV6[31:0] = R6; RV7[31:0] = R7
endmodule
