// Logisim project Ctl_Conditional.circ as structural Verilog: 1 circuit, main circuit Conditional
module Conditional (
  input  Enable,
  input  [15:0] Instruction,
  input  Z,
  input  C,
  input  N,
  input  V,
  output [10:0] Offset,
  output Verified
);

  wire and_1_out, GE, GT, HI, LE, LS, multiplexer_3_out, not_1_out, not_2_out, not_3_out, not_4_out,
       not_5_out, not_6_out, not_7_out, not_8_out, not_9_out, sortie;
  wire [10:0] imm8_11bits, multiplexer_1_out;

  assign imm8_11bits = {{3{Instruction[7]}}, Instruction[7:0]};  // Bit_Extender bit_extender_1
  Comparator #(.width(1)) comparator_1 (.a(N), .b(V), .eq(GE));  // open: gt, lt
  Multiplexer #(.width(11)) multiplexer_1 (
    .in0(imm8_11bits), .in1(Instruction[10:0]), .out(multiplexer_1_out), .sel(Instruction[13]));
  Multiplexer #(.width(11)) multiplexer_2 (.in0({11{1'b0}}), .in1(multiplexer_1_out), .out(Offset), .sel(and_1_out));
  and and_1 (and_1_out, Enable, Verified);
  Multiplexer multiplexer_3 (.in0(sortie), .in1(1'b1), .out(multiplexer_3_out), .sel(Instruction[13]));
  and and_2 (HI, C, not_1_out);
  not not_1 (not_1_out, Z);
  not not_2 (not_2_out, Z);
  and and_3 (GT, not_2_out, GE);
  Multiplexer multiplexer_4 (.in0(1'b0), .in1(multiplexer_3_out), .out(Verified), .sel(Enable));
  not not_3 (not_3_out, C);
  not not_4 (not_4_out, GE);
  or or_1 (LS, not_3_out, Z);
  or or_2 (LE, Z, not_4_out);
  not not_5 (not_5_out, Z);
  not not_6 (not_6_out, C);
  not not_7 (not_7_out, N);
  not not_8 (not_8_out, V);
  Multiplexer #(.select(4)) multiplexer_5 (
    .in0(Z), .in1(not_5_out), .in2(C), .in3(not_6_out), .in4(N), .in5(not_7_out), .in6(V), .in7(not_8_out),
    .in8(HI), .in9(LS), .in10(GE), .in11(not_9_out), .in12(GT), .in13(LE), .in14(1'b1), .in15(1'b0),
    .out(sortie), .sel(Instruction[11:8]));
  not not_9 (not_9_out, GE);

  // Other names for the same wires on the sheet: imm8[7:0] = Instruction[7:0]; imm11[10:0] = Instruction[10:0];
  //   cond[3:0] = Instruction[11:8]; treize = Instruction[13]
endmodule
