// Logisim project Ctl_Flags_APSR.circ as structural Verilog: 1 circuit, main circuit Flags_APSR
module Flags_APSR (
  input  [3:0] Update_Mask,
  input  [3:0] Flags_In,
  input  Clk,
  input  Rst,
  output [3:0] Flags_Out
);

  Register #(.width(1)) R2 (.D(Flags_In[2]), .en(Update_Mask[2]), .clk(Clk), .Q(Flags_Out[2]), .clr(Rst));
  Register #(.width(1)) R0 (.D(Flags_In[0]), .en(Update_Mask[0]), .clk(Clk), .Q(Flags_Out[0]), .clr(Rst));
  Register #(.width(1)) R3 (.D(Flags_In[3]), .en(Update_Mask[3]), .clk(Clk), .Q(Flags_Out[3]), .clr(Rst));
  Register #(.width(1)) R1 (.D(Flags_In[1]), .en(Update_Mask[1]), .clk(Clk), .Q(Flags_Out[1]), .clr(Rst));

  // Other names for the same wires on the sheet: D0 = Flags_In[0]; D1 = Flags_In[1]; D2 = Flags_In[2];
  //   D3 = Flags_In[3]; S0 = Flags_Out[0]; S1 = Flags_Out[1]; S2 = Flags_Out[2]; S3 = Flags_Out[3];
  //   M0 = Update_Mask[0]; M1 = Update_Mask[1]; M2 = Update_Mask[2]; M3 = Update_Mask[3]
endmodule
