// Logisim project Ctl_Load_Store.circ as structural Verilog: 1 circuit, main circuit Load_Store
module Load_Store (
  input  [15:0] Instruction,
  input  Enable,
  input  Clk,
  input  Reset,
  input  [31:0] Stack_Pointer,
  output [2:0] Rmd,
  output [31:0] RAM_Addr,
  output Load,
  output PC_Hold,
  output Store
);

  wire and_3_out, comparator_1_eq, comparator_1_lt, d_ff_1_q, not_1_out;
  wire [31:0] adder_1_out, bit_extender_1_out;

  Comparator #(.width(1)) comparator_1 (
    .a(1'b1), .b(Instruction[11]), .eq(comparator_1_eq), .lt(comparator_1_lt));  // open: gt
  assign bit_extender_1_out = {{24{1'b0}}, Instruction[7:0]};  // Bit_Extender bit_extender_1
  and and_1 (Store, Enable, comparator_1_lt);
  Adder #(.width(32)) adder_1 (.a(Stack_Pointer), .b(bit_extender_1_out), .out(adder_1_out));  // open: cin, cout
  and and_2 (Load, Enable, comparator_1_eq);
  Multiplexer #(.width(32)) multiplexer_1 (.in0({32{1'b0}}), .in1(adder_1_out), .out(RAM_Addr), .sel(Enable));
  not not_1 (not_1_out, d_ff_1_q);
  D_Flip_Flop d_ff_1 (.D(and_3_out), .clk(Clk), .Q(d_ff_1_q), .reset(Reset));  // open: Qn, preset
  and and_3 (and_3_out, not_1_out, Load);
  Multiplexer #(.width(3)) multiplexer_2 (.in0(3'b000), .in1(Instruction[10:8]), .out(Rmd), .sel(Enable));
  Multiplexer multiplexer_3 (.in0(1'b0), .in1(d_ff_1_q), .out(PC_Hold), .sel(Enable));

  // Other names for the same wires on the sheet: rt[2:0] = Instruction[10:8]; SP[31:0] = Stack_Pointer

  // Notes on the sheet:
  //   Instruction: pull=down
  //   Delay load and hold PC for 1 cycle for the RAM to send out requested data 
endmodule
