// Logisim project Ctl_SP_Address.circ as structural Verilog: 1 circuit, main circuit SP_Address
module SP_Address (
  input  [31:0] Stack_Pointer,
  input  [15:0] Instruction,
  input  Enable,
  output [31:0] New_Stack_Pointer,
  output Write_Enable
);

  wire [31:0] adder_1_out, imm7_etendu, multiplexer_1_out, subtractor_1_out;

  assign imm7_etendu = {{25{1'b0}}, Instruction[6:0]};  // Bit_Extender bit_extender_1
  Adder #(.width(32)) adder_1 (.a(Stack_Pointer), .b(imm7_etendu), .out(adder_1_out));  // open: cin, cout
  Subtractor #(.width(32)) subtractor_1 (
    .a(Stack_Pointer), .b(imm7_etendu), .out(subtractor_1_out));  // open: bin, bout
  Multiplexer #(.width(32)) multiplexer_1 (
    .in0(adder_1_out), .in1(subtractor_1_out), .out(multiplexer_1_out), .sel(Instruction[7]));
  and and_1 (Write_Enable, Enable, 1'b1);
  Multiplexer #(.width(32)) multiplexer_2 (
    .in0({32{1'b0}}), .in1(multiplexer_1_out), .out(New_Stack_Pointer), .sel(Enable));

  // Other names for the same wires on the sheet: imm7[6:0] = Instruction[6:0]; Bit7 = Instruction[7]

  // Notes on the sheet:
  //   Pull output low on Enable = 0
endmodule
