// Logisim project Ctl_Shift_Add_Sub_Mov.circ as structural Verilog: 1 circuit, main circuit Shift_Add_Sub_Mov
module Shift_Add_Sub_Mov (
  input  Enable,
  input  [15:0] Instruction,
  output [3:0] Flags_Update_Mask,
  output Carry,
  output Imm32_Enable,
  output [2:0] Rm,
  output [2:0] Rn,
  output [2:0] Rd,
  output [4:0] Imm5,
  output [31:0] Imm32,
  output [3:0] ALU_Opcode
);

  wire and_1_out, and_2_out, and_3_out, and_4_out, and_5_out, and_6_out, and_7_out, and_8_out, and_9_out,
       and_10_out, and_11_out, and_12_out, and_14_out, C, carry_t, Imm32_enable_t, isMov, or_2_out, or_3_out,
       or_6_out, RN_SHIFT;
  wire [0:0] Flags;
  wire [2:0] multiplexer_2_out, RD_t, RM_t, RN_t;
  wire [3:0] ADD_OR_SUB, AluCodop;
  wire [4:0] Imm_5;
  wire [31:0] bit_extender_1_out, bit_extender_2_out, Imm_32, multiplexer_18_out, multiplexer_19_out,
       negator_1_out;

  Multiplexer #(.width(3)) multiplexer_1 (
    .in0(Instruction[2:0]), .in1(Instruction[10:8]), .out(RD_t), .sel(Instruction[13]));
  and and_1 (and_1_out, ~Instruction[11], ~Instruction[12], ~Instruction[13]);  // AND_Gate
  and and_2 (and_2_out, Instruction[11], ~Instruction[12], ~Instruction[13]);  // AND_Gate
  and and_3 (and_3_out, ~Instruction[11], Instruction[12], ~Instruction[13]);  // AND_Gate
  Multiplexer #(.width(3)) multiplexer_2 (
    .in0(3'b000), .in1(Instruction[10:8]), .out(multiplexer_2_out), .sel(and_4_out));
  and and_4 (and_4_out, Instruction[12], Instruction[13]);
  or or_1 (RN_SHIFT, and_1_out, and_2_out, and_3_out);
  Multiplexer #(.width(3)) multiplexer_3 (.in0(3'b000), .in1(RM_t), .out(Rm), .sel(Enable));
  Multiplexer #(.width(3)) multiplexer_4 (.in0(3'b000), .in1(RN_t), .out(Rn), .sel(Enable));
  Multiplexer #(.width(3)) multiplexer_5 (.in0(3'b000), .in1(RD_t), .out(Rd), .sel(Enable));
  and and_5 (and_5_out, Instruction[11], Instruction[12], ~Instruction[13]);  // AND_Gate
  Multiplexer #(.width(4)) multiplexer_6 (
    .in0(4'b0000), .in1({2'b11, C, Flags[0]}), .out(Flags_Update_Mask), .sel(Enable));
  Multiplexer multiplexer_7 (.in0(1'b0), .in1(carry_t), .out(Carry), .sel(Enable));
  Multiplexer multiplexer_8 (.in0(1'b0), .in1(Imm32_enable_t), .out(Imm32_Enable), .sel(Enable));
  Multiplexer #(.width(5)) multiplexer_9 (.in0({5{1'b0}}), .in1(Imm_5), .out(Imm5), .sel(Enable));
  Multiplexer #(.width(32)) multiplexer_10 (.in0({32{1'b0}}), .in1(Imm_32), .out(Imm32), .sel(Enable));
  Multiplexer #(.width(4)) multiplexer_11 (.in0(4'b0000), .in1(AluCodop), .out(ALU_Opcode), .sel(Enable));
  or or_2 (or_2_out, and_5_out, RN_SHIFT);
  Multiplexer #(.width(3)) multiplexer_12 (.in0(multiplexer_2_out), .in1(Instruction[5:3]), .out(RN_t), .sel(or_2_out));
  Multiplexer #(.width(3)) multiplexer_13 (.in0(Instruction[8:6]), .in1(3'b000), .out(RM_t), .sel(Instruction[10]));
  and and_6 (and_6_out, Instruction[11], Instruction[12], Instruction[13]);
  and and_7 (and_7_out, Instruction[11], Instruction[12], Instruction[9]);
  or or_3 (or_3_out, and_6_out, and_7_out);
  or or_4 (C, Instruction[11], Instruction[12], ~Instruction[13]);  // OR_Gate
  and and_8 (and_8_out, Instruction[11], Instruction[12]);
  and and_9 (and_9_out, Instruction[13], Instruction[12]);
  and and_10 (and_10_out, Instruction[13], Instruction[11]);
  Multiplexer multiplexer_14 (.in0(1'b0), .in1(1'b1), .out(carry_t), .sel(or_3_out));
  Multiplexer #(.width(4)) multiplexer_15 (.in0(4'b0101), .in1(4'b0110), .out(ADD_OR_SUB), .sel(Instruction[9]));
  and and_11 (and_11_out, ~Instruction[11], ~Instruction[13]);  // AND_Gate
  and and_12 (and_12_out, ~Instruction[13], ~Instruction[12]);  // AND_Gate
  or or_5 (Flags[0], and_8_out, and_9_out, and_10_out);
  Multiplexer #(.width(5)) multiplexer_16 (.in0({5{1'b0}}), .in1(Instruction[10:6]), .out(Imm_5), .sel(or_6_out));
  or or_6 (or_6_out, and_11_out, and_12_out);
  Multiplexer #(.select(3), .width(4)) multiplexer_17 (
    .in0(4'b0010), .in1(4'b0011), .in2(4'b0100), .in3(ADD_OR_SUB), .in4(4'b1001), .in5(4'b1010),
    .in6(4'b0101), .in7(4'b0110), .out(AluCodop), .sel(Instruction[13:11]));
  assign bit_extender_1_out = {{24{1'b0}}, Instruction[7:0]};  // Bit_Extender bit_extender_1
  Negator #(.width(32)) negator_1 (.in(bit_extender_1_out), .out(negator_1_out));
  and and_13 (isMov, ~Instruction[11], ~Instruction[12], Instruction[13]);  // AND_Gate
  assign bit_extender_2_out = {{29{1'b0}}, Instruction[8:6]};  // Bit_Extender bit_extender_2
  Multiplexer #(.width(32)) multiplexer_18 (
    .in0(bit_extender_1_out), .in1(negator_1_out), .out(multiplexer_18_out), .sel(isMov));
  and and_14 (and_14_out, Instruction[11], Instruction[12], Instruction[10]);
  Multiplexer #(.width(32)) multiplexer_19 (
    .in0(bit_extender_2_out), .in1(multiplexer_18_out), .out(multiplexer_19_out), .sel(Instruction[13]));
  or or_7 (Imm32_enable_t, and_14_out, Instruction[13]);
  Multiplexer #(.width(32)) multiplexer_20 (
    .in0({32{1'b0}}), .in1(multiplexer_19_out), .out(Imm_32), .sel(Imm32_enable_t));

  // Other names for the same wires on the sheet: V = Flags[0]; Flags[1] = C; Bits_0_2[2:0] = Instruction[2:0];
  //   Bits_0_7[7:0] = Instruction[7:0]; Bits_3_5[2:0] = Instruction[5:3]; Bits_6_8[2:0] = Instruction[8:6];
  //   Bits_6_10[4:0] = Instruction[10:6]; Bits_8_10[2:0] = Instruction[10:8]; Bit_9 = Instruction[9];
  //   Bit_10 = Instruction[10]; Bit_11 = Instruction[11]; Bits_11_12[1:0] = Instruction[12:11];
  //   Bits_11_13[2:0] = Instruction[13:11]; Bit_12 = Instruction[12]; Bit_13 = Instruction[13];
  //   Bits_13_15[2:0] = Instruction[15:13]

  // Notes on the sheet:
  //   Note: ALU uses Rn register for shifts. Use Rn instead of Rm for shifts (immediate) here too
  //   Note 3: Imm32_Enable forces the use of the immediate for Rm register
  //   Note 2: MOV uses RSB ALU opcode with Imm8 reversed so that it is copied to output register
  //   Pull output low on Enable = 0
  //   only ADD and SUB use Rm
  //   Enable carry for SUB since it is reversed in ALU
  //   ALU will use Imm32 instead of Rm
endmodule
